# Fritzing sketch SmartPlug (saved by Fritzing 0.9.5d)
circuit board: 15.1821cm x 7.45189cm

parts:
  J1 = 220v plug
  Mod1 = generic-ac-power-supply [package=THT]
  M1 = DOIT Esp32 DevKit v1 (30 pins long, 11 pins width) [part_number=ESP32S-PIN30]
  U1 = 2-Channel 5v Relay Shield [package=relay-2ch5v10a]
  J2 = 120V duplex outlet_1

nets:
  N1: J1.pin1, Mod1.pin1, J2.H2
  N2: J1.pin2, Mod1.pin2, U1.K2-In
  N3: Mod1.pin3#2, M1.VIN
  N4: Mod1.pin3#3, M1.GND
  N5: M1.D27, U1.IN2
  N6: M1.D14, U1.IN1
  N7: U1.K1-Off, J2.N2
  N8: U1.K2-Off, U1.K2-On

custom parts:
  220v plug: Generic 220V AC plug.
  generic-ac-power-supply: Generic ac power supply module. Use as is, or customize the svgs to fit your particular device (as they are all different.) Provides AC input and single DC output. PCB is generic and will need modifications if you intend to do a pcb mount.
  DOIT Esp32 DevKit v1 (30 pins long, 11 pins width): The DOIT Esp32 DevKit v1 is one of the development board created by DOIT to evaluate the ESP-WROOM-32 module. It is based on the ESP32 microcontroller that boasts Wifi, Bluetooth, Ethernet and Low Power support all in a single chip. (vanepp) made breadboard work, adjusted pin numbering and labels and reduced size of schematic and cleaned up pcb. This chip is 30pins long (2 x15) and 11 pins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
  2-Channel 5v Relay Shield: 2 Channel 5v Relay Shield w. 2x SPD-06VDC-SD-C
  120V duplex outlet_1: 120V duplex outlet.
